// Logisim project 3_ALU.circ as structural Verilog: 9 circuits, main circuit halfadder
module halfadder (
  input  a,
  input  b,
  output s,
  output c
);

  xor xor_1 (s, a, b);
  and and_1 (c, a, b);
endmodule

module fulladder_1 (
  input  a,
  input  b,
  input  ci,
  output co,
  output S
);

  wire halfadder_1_c, halfadder_1_s, halfadder_2_c;

  halfadder halfadder_1 (.a(a), .b(b), .s(halfadder_1_s), .c(halfadder_1_c));
  halfadder halfadder_2 (.a(halfadder_1_s), .b(ci), .s(S), .c(halfadder_2_c));
  or or_1 (co, halfadder_1_c, halfadder_2_c);
endmodule

module fa_4 (
  input  [3:0] a,
  input  [3:0] b,
  input  ci,
  output co,
  output [3:0] s
);

  wire fulladder_1_2_co, fulladder_1_3_co, fulladder_1_4_co;

  fulladder_1 fulladder_1_1 (.a(a[3]), .b(b[3]), .ci(fulladder_1_2_co), .co(co), .S(s[3]));
  fulladder_1 fulladder_1_2 (.a(a[2]), .b(b[2]), .ci(fulladder_1_3_co), .co(fulladder_1_2_co), .S(s[2]));
  fulladder_1 fulladder_1_3 (.a(a[1]), .b(b[1]), .ci(fulladder_1_4_co), .co(fulladder_1_3_co), .S(s[1]));
  fulladder_1 fulladder_1_4 (.a(a[0]), .b(b[0]), .ci(ci), .co(fulladder_1_4_co), .S(s[0]));
endmodule

module fa_16 (
  input  [15:0] a,
  input  [15:0] b,
  input  ci,
  output co,
  output [15:0] s
);

  wire fa_4_2_co, fa_4_3_co, fa_4_4_co;

  fa_4 fa_4_1 (.a(a[15:12]), .b(b[15:12]), .ci(fa_4_2_co), .co(co), .s(s[15:12]));
  fa_4 fa_4_2 (.a(a[11:8]), .b(b[11:8]), .ci(fa_4_3_co), .co(fa_4_2_co), .s(s[11:8]));
  fa_4 fa_4_3 (.a(a[7:4]), .b(b[7:4]), .ci(fa_4_4_co), .co(fa_4_3_co), .s(s[7:4]));
  fa_4 fa_4_4 (.a(a[3:0]), .b(b[3:0]), .ci(ci), .co(fa_4_4_co), .s(s[3:0]));
endmodule

module fa_32 (
  input  [31:0] a,
  input  [31:0] b,
  input  ci,
  output co,
  output [31:0] s
);

  wire fa_16_2_co;

  fa_16 fa_16_1 (.a(a[31:16]), .b(b[31:16]), .ci(fa_16_2_co), .co(co), .s(s[31:16]));
  fa_16 fa_16_2 (.a(a[15:0]), .b(b[15:0]), .ci(ci), .co(fa_16_2_co), .s(s[15:0]));
endmodule

module mul_32 (
  input  [31:0] a,
  input  [31:0] b,
  input  u,
  output [31:0] s,
  output [31:0] co
);

  wire [31:0] multiplier_1_cout, multiplier_1_out, multiplier_2_cout, multiplier_2_out;

  Multiplier #(.mode("twosComplement"), .width(32)) multiplier_1 (
    .a(a), .b(b), .out(multiplier_1_out), .cin({32{1'b0}}), .cout(multiplier_1_cout));
  Multiplier #(.mode("twosComplement"), .width(32)) multiplier_2 (
    .a(a), .b(b), .out(multiplier_2_out), .cin({32{1'b0}}), .cout(multiplier_2_cout));
  Multiplexer #(.width(32)) multiplexer_1 (.in0(multiplier_1_out), .in1(multiplier_2_out), .out(s), .sel(u));
  Multiplexer #(.width(32)) multiplexer_2 (.in0(multiplier_2_cout), .in1(multiplier_1_cout), .out(co), .sel(u));
endmodule

module div_32 (
  input  [31:0] a,
  input  [31:0] b,
  input  u,
  output [31:0] ans,
  output [31:0] rem_o
);

  wire [31:0] divider_1_out, divider_1_rem, divider_2_out, divider_2_rem;

  Divider #(.mode("twosComplement"), .width(32)) divider_1 (
    .a(a), .b(b), .out(divider_1_out), .upper({32{1'b0}}), .rem(divider_1_rem));
  Divider #(.width(32)) divider_2 (.a(a), .b(b), .out(divider_2_out), .upper({32{1'b0}}), .rem(divider_2_rem));
  Multiplexer #(.width(32)) multiplexer_1 (.in0(divider_1_rem), .in1(divider_2_rem), .out(rem_o), .sel(u));
  Multiplexer #(.width(32)) multiplexer_2 (.in0(divider_1_out), .in1(divider_2_out), .out(ans), .sel(u));
endmodule

module sub_32 (
  input  lend,
  input  [31:0] a,
  input  [31:0] b,
  output [31:0] ans,
  output borrow
);

  Subtractor #(.width(32)) subtractor_1 (.a(a), .b(b), .out(ans), .bin(lend), .bout(borrow));
endmodule

module ALU (
  input  [31:0] a,
  input  [31:0] b,
  input  u,
  input  [3:0] ord,
  output [31:0] result1,
  output [31:0] result2
);

  wire comparator_1_eq, comparator_2_lt, comparator_3_lt, fa_32_1_co, sub_32_1_borrow;
  wire [31:0] and_1_out, bit_extender_1_out, bit_extender_2_out, bit_extender_3_out, bit_extender_4_out,
       bit_extender_5_out, div_32_1_ans, div_32_1_rem_o, fa_32_1_s, mul_32_1_co, mul_32_1_s, nor_1_out,
       or_1_out, shifter_1_out, shifter_2_out, shifter_3_out, sub_32_1_ans, xor_1_out;

  assign and_1_out = a & b;  // AND_Gate and_1, 32 bits wide
  assign or_1_out = a | b;  // OR_Gate or_1, 32 bits wide
  assign xor_1_out = a ^ b;  // XOR_Gate xor_1, 32 bits wide
  assign nor_1_out = ~(a | b);  // NOR_Gate nor_1, 32 bits wide
  Comparator #(.width(32)) comparator_1 (.a(a), .b(b), .eq(comparator_1_eq));  // open: gt, lt
  Comparator #(.width(32)) comparator_2 (.a(a), .b(b), .lt(comparator_2_lt));  // open: gt, eq
  Comparator #(.mode("unsigned"), .width(32)) comparator_3 (.a(a), .b(b), .lt(comparator_3_lt));  // open: gt, eq
  Shifter #(.width(32)) shifter_1 (.in(b), .\dist (a[4:0]), .out(shifter_1_out));
  Shifter #(.shift("ar"), .width(32)) shifter_2 (.in(b), .\dist (a[4:0]), .out(shifter_2_out));
  Shifter #(.shift("lr"), .width(32)) shifter_3 (.in(b), .\dist (a[4:0]), .out(shifter_3_out));
  assign bit_extender_1_out = {{31{comparator_1_eq}}, comparator_1_eq};  // Bit_Extender bit_extender_1
  mul_32 mul_32_1 (.a(a), .b(b), .u(u), .s(mul_32_1_s), .co(mul_32_1_co));
  div_32 div_32_1 (.a(a), .b(b), .u(u), .ans(div_32_1_ans), .rem_o(div_32_1_rem_o));
  fa_32 fa_32_1 (.a(a), .b(b), .ci(1'b0), .co(fa_32_1_co), .s(fa_32_1_s));
  sub_32 sub_32_1 (.lend(1'b0), .a(a), .b(b), .ans(sub_32_1_ans), .borrow(sub_32_1_borrow));
  assign bit_extender_2_out = {{31{1'b0}}, comparator_2_lt};  // Bit_Extender bit_extender_2
  assign bit_extender_3_out = {{31{1'b0}}, comparator_3_lt};  // Bit_Extender bit_extender_3
  assign bit_extender_4_out = {{31{fa_32_1_co}}, fa_32_1_co};  // Bit_Extender bit_extender_4
  assign bit_extender_5_out = {{31{sub_32_1_borrow}}, sub_32_1_borrow};  // Bit_Extender bit_extender_5
  Multiplexer #(.select(4), .width(32)) multiplexer_1 (
    .in0(shifter_1_out), .in1(shifter_2_out), .in2(shifter_3_out), .in3(mul_32_1_s), .in4(div_32_1_ans),
    .in5(fa_32_1_s), .in6(sub_32_1_ans), .in7(and_1_out), .in8(or_1_out), .in9(xor_1_out), .in10(nor_1_out),
    .in11(bit_extender_1_out), .in12(bit_extender_2_out), .in13(bit_extender_3_out), .out(result1), .sel(ord));  // open: in14, in15
  Multiplexer #(.select(4), .width(32)) multiplexer_2 (
    .in0({32{1'b0}}), .in1({32{1'b0}}), .in2({32{1'b0}}), .in3(mul_32_1_co), .in4(div_32_1_rem_o),
    .in5(bit_extender_4_out), .in6(bit_extender_5_out), .out(result2), .sel(ord));  // open: in7, in8, in9, in10, in11, in12, in13, in14, in15
endmodule
