// Logisim project controller.circ as structural Verilog: 1 circuit, main circuit ID
module ID (
  input  [5:0] op,
  input  [5:0] func,
  output RegDst,
  output ALUSrc,
  output MemRead,
  output Memwrite,
  output MemtoReg1,
  output MemtoReg2,
  output EXTOp,
  output Branch,
  output [3:0] ALUOp,
  output EXTOp2,
  output [1:0] DMSel,
  output U,
  output SHAMT,
  output NEQ,
  output RegWrite,
  output [1:0] J,
  output MorD
);

  wire and_4_out, and_5_out, and_9_out, and_10_out, and_11_out, and_12_out, and_13_out, and_14_out,
       and_15_out, and_16_out, and_17_out, and_18_out, and_19_out, and_20_out, and_21_out, and_22_out,
       and_23_out, and_24_out, and_25_out, and_26_out, and_27_out, and_28_out, and_29_out, and_30_out,
       and_31_out, and_32_out, and_33_out, and_37_out, and_38_out, and_41_out, and_42_out, and_43_out,
       and_44_out, not_1_out, not_2_out, not_3_out, not_4_out, not_5_out, not_6_out, not_7_out, not_8_out,
       not_9_out, not_10_out, not_11_out;

  not not_1 (not_1_out, op[5]);
  not not_2 (not_2_out, op[3]);
  not not_3 (not_3_out, op[2]);
  not not_4 (not_4_out, op[1]);
  not not_5 (not_5_out, op[0]);
  not not_6 (not_6_out, func[5]);
  not not_7 (not_7_out, func[4]);
  not not_8 (not_8_out, func[3]);
  not not_9 (not_9_out, func[2]);
  not not_10 (not_10_out, func[1]);
  not not_11 (not_11_out, func[0]);
  and and_1 (RegDst, not_1_out, not_2_out, not_3_out, not_4_out, not_8_out);
  or or_1 (ALUSrc, op[5], op[3]);
  and and_2 (MemRead, op[5], not_2_out);
  and and_3 (Memwrite, op[5], op[3]);
  and and_4 (and_4_out, op[5], not_2_out);
  and and_5 (and_5_out, op[2], op[1], op[0]);
  and and_6 (MemtoReg2, op[2], op[1], op[0]);
  and and_7 (EXTOp, op[3], op[2], not_4_out, not_5_out);
  and and_8 (Branch, not_1_out, not_2_out, op[2]);
  and and_9 (and_9_out, not_1_out, not_2_out, not_4_out, func[5], func[2], func[1]);
  and and_10 (and_10_out, not_1_out, not_2_out, op[2]);
  and and_11 (and_11_out, not_1_out, op[3], not_3_out, op[1]);
  and and_12 (and_12_out, not_1_out, not_2_out, not_4_out, func[2], not_10_out, func[0]);
  and and_13 (and_13_out, not_1_out, op[2], not_4_out, op[0]);
  and and_14 (and_14_out, op[2], op[1], not_5_out);
  and and_15 (and_15_out, not_3_out, not_4_out, func[5], not_9_out);
  and and_16 (and_16_out, not_3_out, not_4_out, func[5], not_10_out, not_11_out);
  and and_17 (and_17_out, op[3], not_3_out);
  and and_18 (and_18_out, op[3], not_4_out, not_5_out);
  and and_19 (and_19_out, not_3_out, not_4_out, func[3], func[1]);
  and and_20 (and_20_out, not_1_out, not_2_out, not_4_out, func[4], not_10_out);
  and and_21 (and_21_out, not_1_out, not_2_out, not_4_out, func[5], not_10_out, not_11_out);
  and and_22 (and_22_out, not_1_out, not_2_out, not_4_out, func[5], func[1], func[0]);
  and and_23 (and_23_out, not_1_out, op[2], not_4_out, not_5_out);
  and and_24 (and_24_out, not_1_out, not_2_out, op[2]);
  and and_25 (and_25_out, not_1_out, not_2_out, not_4_out, func[5], not_9_out);
  and and_26 (and_26_out, not_1_out, not_2_out, not_4_out, not_6_out, not_7_out, func[1], not_11_out);
  and and_27 (and_27_out, op[3], not_3_out, op[0]);
  and and_28 (and_28_out, op[2], not_5_out);
  and and_29 (and_29_out, not_4_out, not_5_out, not_6_out, not_7_out, func[0]);
  and and_30 (and_30_out, not_4_out, not_5_out, func[4], not_10_out);
  and and_31 (and_31_out, not_4_out, not_5_out, func[5], func[2], not_11_out);
  and and_32 (and_32_out, not_2_out, not_4_out, op[0]);
  and and_33 (and_33_out, op[3], not_4_out, not_5_out);
  and and_34 (EXTOp2, op[5], op[2]);
  and and_35 (DMSel[1], op[5], not_2_out, op[1]);
  and and_36 (DMSel[0], op[5], not_2_out, not_4_out, op[0]);
  and and_37 (and_37_out, not_1_out, not_2_out, not_3_out, not_4_out, func[5], not_9_out, func[0]);
  and and_38 (and_38_out, not_1_out, not_3_out, not_4_out, op[0]);
  and and_39 (SHAMT, not_1_out, not_2_out, not_3_out, not_4_out, not_6_out, not_8_out, not_9_out);
  and and_40 (NEQ, not_1_out, not_2_out, not_4_out, op[0]);
  and and_41 (and_41_out, not_1_out, op[3]);
  and and_42 (and_42_out, not_2_out, not_3_out, not_4_out, not_8_out);
  and and_43 (and_43_out, not_2_out, not_3_out, op[0]);
  and and_44 (and_44_out, op[5], not_2_out, not_5_out);
  and and_45 (J[1], not_1_out, not_2_out, not_3_out, not_4_out, not_7_out, func[3]);
  and and_46 (J[0], not_1_out, not_2_out, op[1]);
  and and_47 (MorD, not_1_out, not_2_out, not_3_out, not_4_out, func[4]);
  or or_2 (MemtoReg1, and_4_out, and_5_out);
  or or_3 (ALUOp[3], and_9_out, and_10_out, and_11_out, and_12_out, and_13_out, and_14_out);
  or or_4 (ALUOp[2], op[5], and_15_out, and_16_out, and_17_out, and_18_out, and_19_out);
  or or_5 (ALUOp[1], and_20_out, and_21_out, and_22_out, and_23_out, and_24_out, and_25_out, and_26_out);
  or or_6 (U, and_37_out, and_38_out);
  or or_7 (RegWrite, and_41_out, and_42_out, and_43_out, and_44_out);
  or or_8 (ALUOp[0], op[5], and_27_out, and_28_out, and_29_out, and_30_out, and_31_out, and_32_out, and_33_out);
endmodule
