// Logisim project cpu_39.circ as structural Verilog: 1 circuit, main circuit cpu
module cpu (
  input  in_1,
  output [3:0] out_2,
  output [31:0] out_3,
  output [31:0] LO_D,
  output [31:0] HI_D,
  output [31:0] out_6,
  output ERR
);

  wire ALUSrc, and_2_out, branch, clk, counter_1_carry, counter_2_carry, counter_3_carry, counter_4_carry,
       DM_clk, extop, extop2, lo_hi_clk, MemRead, MemtoReg1, MemtoReg2, MemWrite, MorD, NEQ, not_1_out,
       not_2_out, REG_clk, RegDst, RegWrite, shamt, U, xor_1_out;
  wire [1:0] DMSel, J, s_offset;
  wire [2:0] counter_2_q, counter_3_q, counter_4_q;
  wire [4:0] alu_1_result1, im_1_p1, multiplexer_1_out, multiplexer_2_out, undriven;
  wire [7:0] bitselector_1_out;
  wire [15:0] bitselector_2_out;
  wire [27:0] multiplexer_7_out;
  wire [30:0] alu_1_result2;
  wire [31:0] adder_1_out, adder_2_out, bit_extender_1_out, bit_extender_2_out, bit_extender_3_out,
       bit_extender_4_out, bit_extender_5_out, bit_extender_6_out, bit_extender_7_out, bit_extender_8_out,
       dm_1_rd, grf_1_rd2, multiplexer_3_out, multiplexer_4_out, multiplexer_5_out, multiplexer_6_out,
       multiplexer_9_out, multiplexer_10_out, multiplexer_11_out, OFFSET, pc_q, R_Addr, R_addr_t,
       shifter_2_out;
  wire [31:7] alu_1_result1_2;
  wire [31:28] multiplexer_7_out_2;
  wire [31:31] alu_1_result2_2;

  Clock clock_1 (.out(clk));
  // IM im_1: pin names not known; wires that end beside it: im_1_p1, out_6
  ID id_1 (
    .op(out_6[31:26]), .func(out_6[5:0]), .RegDst(RegDst), .ALUSrc(ALUSrc), .MemRead(MemRead),
    .Memwrite(MemWrite), .MemtoReg1(MemtoReg1), .MemtoReg2(MemtoReg2), .EXTOp(extop), .Branch(branch),
    .ALUOp(out_2), .EXTOp2(extop2), .DMSel(DMSel), .U(U), .SHAMT(shamt), .NEQ(NEQ), .RegWrite(RegWrite),
    .J(J), .MorD(MorD));
  Multiplexer #(.select(2), .width(5)) multiplexer_1 (
    .in0(out_6[25:21]), .in1(out_6[25:21]), .in2(undriven), .out(multiplexer_1_out));  // open: in3, sel
  Multiplexer #(.width(5)) multiplexer_2 (
    .in0(out_6[20:16]), .in1(out_6[15:11]), .out(multiplexer_2_out), .sel(RegDst));
  assign bit_extender_1_out = {{27{out_6[10]}}, out_6[10:6]};  // Bit_Extender bit_extender_1
  assign bit_extender_2_out = {{16{out_6[15]}}, out_6[15:0]};  // Bit_Extender bit_extender_2
  assign bit_extender_3_out = {{16{1'b0}}, out_6[15:0]};  // Bit_Extender bit_extender_3
  Counter #(.max('h5)) counter_1 (
    .load(1'b0), .count(1'b1), .carry(counter_1_carry), .up(1'b1), .clk(clk), .clr(in_1));  // open: D, Q
  Shifter #(.width(32)) shifter_1 (.in(bit_extender_2_out), .\dist (5'b00010), .out(OFFSET));
  Multiplexer #(.width(32)) multiplexer_3 (
    .in0(bit_extender_2_out), .in1(bit_extender_3_out), .out(multiplexer_3_out), .sel(extop));
  Register #(.width(32)) pc (
    .D(multiplexer_6_out), .Q({pc_q[31:7], im_1_p1, pc_q[1:0]}), .clk(counter_1_carry), .clr(in_1));  // open: en
  GRF grf_1 (
    .WD(out_3), .WE(RegWrite), .WA(multiplexer_2_out), .RA1(multiplexer_1_out), .RA2(out_6[20:16]),
    .clk(REG_clk), .reset(in_1), .RD1(R_addr_t), .RD2(grf_1_rd2));
  Multiplexer #(.width(32)) multiplexer_4 (
    .in0(multiplexer_3_out), .in1(bit_extender_1_out), .out(multiplexer_4_out), .sel(shamt));
  Counter #(.max('h5), .width(3)) counter_2 (
    .load(1'b0), .count(1'b1), .Q({counter_2_q[2], DM_clk, counter_2_q[0]}), .carry(counter_2_carry),
    .up(1'b1), .clk(clk), .clr(in_1));  // open: D
  Multiplexer #(.width(32)) multiplexer_5 (
    .in0(grf_1_rd2), .in1(multiplexer_4_out), .out(multiplexer_5_out), .sel(ALUSrc));
  Multiplexer #(.select(2), .width(32)) multiplexer_6 (
    .in0({multiplexer_7_out_2, multiplexer_7_out}), .in1({multiplexer_7_out_2, out_6[25:0], 2'b00}),
    .in2(R_Addr), .out(multiplexer_6_out), .sel(J));  // open: in3
  Adder #(.width(32)) adder_1 (.a(32'h4), .b({pc_q[31:7], im_1_p1, pc_q[1:0]}), .out(adder_1_out));  // open: cin, cout
  assign bit_extender_4_out = {{16{1'b0}}, out_6[15:0]};  // Bit_Extender bit_extender_4
  Counter #(.max('h5), .width(3)) counter_3 (
    .load(1'b0), .count(1'b1), .Q(counter_3_q), .carry(counter_3_carry), .up(1'b1), .clk(clk), .clr(in_1));  // open: D
  ALU alu_1 (
    .a(R_addr_t), .b(multiplexer_5_out), .u(U), .ord(out_2),
    .result1({alu_1_result1_2, alu_1_result1, s_offset}), .result2({alu_1_result2_2[31], alu_1_result2}));
  and and_1 (REG_clk, counter_3_q[1], counter_3_q[0]);
  Adder #(.width(32)) adder_2 (.a(adder_1_out), .b(OFFSET), .out(adder_2_out));  // open: cin, cout
  and and_2 (and_2_out, xor_1_out, branch);
  xor xor_1 (xor_1_out, alu_1_result2_2[31], NEQ);
  Shifter #(.width(32)) shifter_2 (.in(grf_1_rd2), .\dist ({s_offset, 3'b000}), .out(shifter_2_out));
  Counter #(.max('h5), .width(3)) counter_4 (
    .load(1'b0), .count(1'b1), .Q({counter_4_q[2], lo_hi_clk, counter_4_q[0]}), .carry(counter_4_carry),
    .up(1'b1), .clk(clk), .clr(in_1));  // open: D
  Multiplexer #(.width(32)) multiplexer_7 (
    .in0(adder_1_out), .in1(adder_2_out), .out({multiplexer_7_out_2, multiplexer_7_out}), .sel(and_2_out));
  and and_3 (ERR, alu_1_result2[0], not_1_out, not_2_out);
  not not_1 (not_1_out, U);
  BitSelector #(.group(8), .width(32)) bitselector_1 (.in(dm_1_rd), .out(bitselector_1_out), .sel(s_offset));
  DM dm_1 (
    .Addr(alu_1_result1), .we(MemWrite), .re(MemRead), .clk(DM_clk), .wd(shifter_2_out), .reset(in_1),
    .rd(dm_1_rd));
  BitSelector #(.group(16), .width(32)) bitselector_2 (.in(dm_1_rd), .out(bitselector_2_out), .sel(s_offset[1]));
  Multiplexer #(.select(2), .width(32)) multiplexer_8 (
    .in0({alu_1_result1_2, alu_1_result1, s_offset}), .in1(multiplexer_11_out), .in2(bit_extender_4_out),
    .in3({out_6[15:0], {16{1'b0}}}), .out(out_3), .sel({MemtoReg2, MemtoReg1}));
  not not_2 (not_2_out, MorD);
  assign bit_extender_5_out = {{24{bitselector_1_out[7]}}, bitselector_1_out};  // Bit_Extender bit_extender_5
  assign bit_extender_6_out = {{24{1'b0}}, bitselector_1_out};  // Bit_Extender bit_extender_6
  assign bit_extender_7_out = {{16{bitselector_2_out[15]}}, bitselector_2_out};  // Bit_Extender bit_extender_7
  assign bit_extender_8_out = {{16{1'b0}}, bitselector_2_out};  // Bit_Extender bit_extender_8
  Multiplexer #(.width(32)) multiplexer_9 (
    .in0(bit_extender_5_out), .in1(bit_extender_6_out), .out(multiplexer_9_out), .sel(extop2));
  Multiplexer #(.width(32)) multiplexer_10 (
    .in0(bit_extender_7_out), .in1(bit_extender_8_out), .out(multiplexer_10_out), .sel(extop2));
  Register #(.width(32)) LO (
    .D({alu_1_result1_2, alu_1_result1, s_offset}), .en(MorD), .clk(lo_hi_clk), .Q(LO_D), .clr(in_1));
  Register #(.width(32)) HI (
    .D({alu_1_result2_2[31], alu_1_result2}), .en(MorD), .clk(lo_hi_clk), .Q(HI_D), .clr(in_1));
  Multiplexer #(.select(2), .width(32)) multiplexer_11 (
    .in0(multiplexer_9_out), .in1(multiplexer_10_out), .in2(dm_1_rd), .out(multiplexer_11_out), .sel(DMSel));  // open: in3

  // Other names for the same wires on the sheet: func[5:0] = out_6[5:0]; I_Addr[25:0] = out_6[25:0];
  //   ALUop[3:0] = out_2; RegData[31:0] = out_3; reset = in_1
endmodule
