// Logisim project semiadd.circ as structural Verilog: 9 circuits, main circuit halfadder
module halfadder (
  input  a,
  input  b,
  output s,
  output c
);

  xor xor_1 (s, a, b);
  and and_1 (c, a, b);
endmodule

module fulladder_1 (
  input  a,
  input  b,
  input  ci,
  output co,
  output S
);

  wire halfadder_1_c, halfadder_1_s, halfadder_2_c;

  halfadder halfadder_1 (.a(a), .b(b), .s(halfadder_1_s), .c(halfadder_1_c));
  halfadder halfadder_2 (.a(halfadder_1_s), .b(ci), .s(S), .c(halfadder_2_c));
  or or_1 (co, halfadder_1_c, halfadder_2_c);
endmodule

module fa_4 (
  input  [3:0] a,
  input  [3:0] b,
  input  ci,
  output co,
  output [3:0] s
);

  wire fulladder_1_2_co, fulladder_1_3_co, fulladder_1_4_co;

  fulladder_1 fulladder_1_1 (.a(a[3]), .b(b[3]), .ci(fulladder_1_2_co), .co(co), .S(s[3]));
  fulladder_1 fulladder_1_2 (.a(a[2]), .b(b[2]), .ci(fulladder_1_3_co), .co(fulladder_1_2_co), .S(s[2]));
  fulladder_1 fulladder_1_3 (.a(a[1]), .b(b[1]), .ci(fulladder_1_4_co), .co(fulladder_1_3_co), .S(s[1]));
  fulladder_1 fulladder_1_4 (.a(a[0]), .b(b[0]), .ci(ci), .co(fulladder_1_4_co), .S(s[0]));
endmodule

module fa_16 (
  input  [15:0] a,
  input  [15:0] b,
  input  ci,
  output co,
  output [15:0] s
);

  wire fa_4_2_co, fa_4_3_co, fa_4_4_co;

  fa_4 fa_4_1 (.a(a[15:12]), .b(b[15:12]), .ci(fa_4_2_co), .co(co), .s(s[3:0]));
  fa_4 fa_4_2 (.a(a[11:8]), .b(b[11:8]), .ci(fa_4_3_co), .co(fa_4_2_co), .s(s[7:4]));
  fa_4 fa_4_3 (.a(a[7:4]), .b(b[7:4]), .ci(fa_4_4_co), .co(fa_4_3_co), .s(s[11:8]));
  fa_4 fa_4_4 (.a(a[3:0]), .b(b[3:0]), .ci(ci), .co(fa_4_4_co), .s(s[15:12]));
endmodule

module fa_32 (
  input  [31:0] a,
  input  [31:0] b,
  input  ci,
  output co,
  output [31:0] s
);

  wire fa_16_2_co;

  fa_16 fa_16_1 (.a(a[31:16]), .b(b[31:16]), .ci(fa_16_2_co), .co(co), .s(s[31:16]));
  fa_16 fa_16_2 (.a(a[15:0]), .b(b[15:0]), .ci(ci), .co(fa_16_2_co), .s(s[15:0]));
endmodule

module mul_32 (
  input  [31:0] ci,
  input  [31:0] a,
  input  [31:0] b,
  output [31:0] s,
  output [31:0] co
);

  Multiplier #(.width(32)) multiplier_1 (.a(a), .b(b), .out(s), .cin(ci), .cout(co));
endmodule

module div_32 (
  input  [31:0] rem_i,
  input  [31:0] a,
  input  [31:0] b,
  output [31:0] ans,
  output [31:0] rem_o
);

  Divider #(.width(32)) divider_1 (.a(a), .b(b), .out(ans), .upper(rem_i), .rem(rem_o));
endmodule

module sub_32 (
  input  lend,
  input  [31:0] a,
  input  [31:0] b,
  output [31:0] ans,
  output borrow
);

  Subtractor #(.width(32)) subtractor_1 (.a(a), .b(b), .out(ans), .bin(lend), .bout(borrow));
endmodule

module LRU (
  input  [31:0] d_m_in,
  input  [31:0] a,
  input  [31:0] b,
  input  a_s_in,
  input  [2:0] ord,
  output a_s_out,
  output [31:0] d_m_out,
  output [31:0] out_8
);

  wire [31:0] and_1_out, div_32_1_ans, fa_32_1_s, mul_32_1_s, nor_1_out, or_1_out, sub_32_1_ans, xor_1_out;

  assign and_1_out = a & a;  // AND_Gate and_1, 32 bits wide
  assign or_1_out = a | a;  // OR_Gate or_1, 32 bits wide
  assign xor_1_out = a ^ a;  // XOR_Gate xor_1, 32 bits wide
  assign nor_1_out = ~(a | a);  // NOR_Gate nor_1, 32 bits wide
  mul_32 mul_32_1 (.ci(d_m_in), .a(a), .b(a), .s(mul_32_1_s), .co(d_m_out));
  div_32 div_32_1 (.rem_i(d_m_in), .a(a), .b(a), .ans(div_32_1_ans), .rem_o(d_m_out));
  fa_32 fa_32_1 (.a(a), .b(a), .ci(a_s_in), .co(a_s_out), .s(fa_32_1_s));
  sub_32 sub_32_1 (.lend(a_s_in), .a(a), .b(a), .ans(sub_32_1_ans), .borrow(a_s_out));
  Multiplexer #(.select(3), .width(32)) multiplexer_1 (
    .in0(mul_32_1_s), .in1(div_32_1_ans), .in2(fa_32_1_s), .in3(sub_32_1_ans), .in4(and_1_out),
    .in5(or_1_out), .in6(xor_1_out), .in7(nor_1_out), .out(out_8), .sel(ord));

  assign b = a;
endmodule
